# Fritzing sketch V1_SmartFarm (saved by Fritzing 1.0.2b)
breadboards: 1

parts:
  DHT1 = Humidity and Temperature Sensor DHT11
  R2 = Photocell (LDR) [power=0.25W dark_resistance_@0.01lx=300kΩ light_resistance_@100lx=400Ω luminance=10lx package=THT]
  R3 = Resistor [tolerance=±5% resistance=10k power=0.25W package=THT]
  M1 = DOIT Esp32 DevKit v1 (30 pins long, 11 pins width) [part_number=ESP32S-PIN30]

nets:
  VCC: DHT1.Vcc, R3.Pin_0, M1.3V3
  N1: DHT1.Data-signal, M1.D2
  N2: DHT1.GND_2, M1.GND
  N3: R2.pin_0, R3.Pin_1
  N4: R2.pin_1, M1.D5

custom parts:
  Humidity and Temperature Sensor DHT11: Digital relative humidity & temperature sensor DHT11
  DOIT Esp32 DevKit v1 (30 pins long, 11 pins width): The DOIT Esp32 DevKit v1 is one of the development board created by DOIT to evaluate the ESP-WROOM-32 module. It is based on the ESP32 microcontroller that boasts Wifi, Bluetooth, Ethernet and Low Power support all in a single chip. (vanepp) made breadboard work, adjusted pin numbering and labels and reduced size of schematic and cleaned up pcb. This chip is 30pins long (2 x15) and 11 pins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
